# Fritzing sketch TermostatoControlAnalogico (saved by Fritzing 0.9.2b)
breadboards: 1

parts:
  Parte1 = EDUCIAA
  U1 = RELAY [package=relay-g5q]
  Q1 = NPN-Transistor [package="TO92 [THT]"]
  R1 = Resistor [tolerance=±5% resistance=10k package=THT]
  D1 = Rectifier Diode [part_number=1N4001 package="300 mil [THT]"]
  J1 = Screw terminal - 2 pins [package=THT]
  R2 = Rotary Potentiometer (Small) [maximum_resistance=10kΩ package=THT]
  T1 = LM35 Temperature Sensor [package="TO92 [THT]"]

nets:
  N1: Parte1.P1_2, U1.COIL1, D1.cathode, T1.+Vs
  N2: Parte1.P1_4, Q1.C
  N3: Parte1.P1_9, T1.Vout
  N4: Parte1.P1_12, R2.leg1, T1.GND
  N5: U1.MAIN, J1.pin2
  N6: U1.NO, J1.pin1
  N7: U1.NC, Q1.E, D1.anode
  N8: Q1.B, R1.Pin_1

notes:
  5V
  CH3 Analog
  GPIO0
  Rele OUT
  AGND
  Potenciómetro Simula Tensión de línea
  3.3V DC equivale a 240V AC
  CH2 Analog
  3.3V

custom parts:
  EDUCIAA: EDUCIAA Board
