# Fritzing sketch ProtectorHeladera (saved by Fritzing 0.9.0b)
breadboards: 1

parts:
  Parte1 = educiaa
  U1 = RELAY [package=relay-g5q]
  Q1 = NPN-Transistor [package="TO92 [THT]"]
  R1 = Resistor [tolerance=±5% resistance=10k package=THT]
  D1 = Rectifier Diode [part_number=1N4001 package="300 mil [THT]"]
  J1 = Screw terminal - 2 pins [package=THT]
  R2 = Rotary Potentiometer (Small) [maximum_resistance=10kΩ package=THT]

nets:
  N1: Parte1.connector49, U1.COIL1, D1.cathode, R2.leg1
  N2: Parte1.connector51, Q1.C
  N3: Parte1.connector56, R2.wiper
  N4: Parte1.connector59, R2.leg2
  N5: U1.MAIN, J1.pin2
  N6: U1.NO, J1.pin1
  N7: U1.NC, Q1.E, D1.anode
  N8: Q1.B, R1.Pin_1

notes:
  5V
  CH3 Analog
  GPIO0
  Rele OUT
  AGND
  Potenciómetro Simula Tensión de línea
  3.3V DC equivale a 240V AC
